# Fritzing sketch Lamp (saved by Fritzing 0.8.7b)
breadboards: 1

parts:
  Part1 = Arduino Nano (Rev3.0)
  LED1 = LED - 5mm [color="Red (633nm)" package="5 mm [THT]"]
  LED2 = LED - 5mm [color="Red (633nm)" package="5 mm [THT]"]
  LED3 = LED - 5mm [color="Red (633nm)" package="5 mm [THT]"]
  J1 = Buzzer
  J2 = Buzzer
  PIR1 = PIR sensor
  Part2 = Adafruit MiCS-5524 Gas Sensor [part_number="Adafruit #3199"]
  R1 = Photocell (LDR) [package=THT]
  R2 = Resistor [package="2512 [SMD]"]

nets:
  GND: Part1.GND, LED1.cathode, LED2.cathode, LED3.cathode, J1.pin1, J2.pin1, PIR1.GND, Part2.5.0V, Part2.GND
  N1: Part1.D2, PIR1.SIG
  N2: Part1.D9, J2.pin2
  N3: Part1.D10, J1.pin2
  N4: Part1.D11/MOSI, LED1.anode, LED2.anode, LED3.anode
  5V: Part1.5V, PIR1.VDD
  N5: Part1.A0, Part2.AOUT
  N6: R1.pin_0, R2.Pin_1

custom parts:
  Buzzer: Fixed frequency buzzer
  Adafruit MiCS-5524 Gas Sensor: Give your next sensor project a nose for gasses with the Adafruit MiCS-5524 Gas Sensor Breakout. This breakout makes it easy to use this nice sensor from SGX Sensortech. The MiCS-5524 is a robust MEMS sensor for indoor carbon monoxide and natural gas leakage detection, it's suitable also for indoor air quality monitoring; breath checker and early fire detection. Please note: This sensor is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
